# Fritzing sketch CircuitX (saved by Fritzing 0.9.3b)
breadboards: 1

parts:
  Part1 = Arduino Uno (Rev3)
  5-12V = Power plug
  MOTOR1 = 28BYJ-48 Stepper Motor
  X1 = X113647 Stepper Driver Board [part_number=X113647 package=board]
  Part2 = RFID-RC522-v2
  LCD1 = LCD screen
  R1 = Trimmer Potentiometer [maximum_resistance=10kΩ package=THT]
  J1 = Piezo Speaker
  LED1 = smd LED [color="Red (633nm)" package="0603 [SMD]"]
  S1 = SWITCH-MOMENTARY-2 [package=tactile-pth-12mm]

nets:
  N1: Part1.A0, X1.IN4
  N2: Part1.A1, X1.IN3
  N3: Part1.A2, X1.IN2
  N4: Part1.A3, X1.IN1
  N5: Part1.A4/SDA, LED1.anode
  N6: Part1.A5/SCL, J1.pin2
  N7: Part1.D8, S1.1
  N8: Part1.D9_PWM, Part2.RST
  N9: Part1.D10_PWM/SS, Part2.SDA
  N10: Part1.D11_PWM/MOSI, Part2.MOSI
  N11: Part1.D12/MISO, Part2.MISO
  N12: Part1.D13/SCK, Part2.SCK
  N13: Part1.D2, LCD1.DB7
  N14: Part1.D3_PWM, LCD1.DB6
  N15: Part1.D4, LCD1.DB5
  N16: Part1.D5_PWM, LCD1.DB4
  N17: Part1.D6_PWM, LCD1.E
  N18: Part1.D7, LCD1.RS
  N19: Part1.3V3, Part2.3_3V
  VCC: Part1.5V, LCD1.LED+, R1.leg2
  GND: Part1.GND, 5-12V.GND, X1.GND, Part2.GND, LCD1.LED-, R1.leg1, J1.pin1, LED1.cathode, S1.2
  HVCC: 5-12V.VCC, X1.+V
  N20: MOTOR1.BLUE, X1.BLUE
  N21: MOTOR1.PINK, X1.PINK
  N22: MOTOR1.RED, X1.YELLOW
  N23: MOTOR1.ORANGE, X1.ORANGE
  N24: MOTOR1.YELLOW, X1.RED
  N25: LCD1.V0, R1.wiper

custom parts:
  28BYJ-48 Stepper Motor: 28BYJ-48 gear-reduction stepper motor (small)
  X113647 Stepper Driver Board: A common stepper motor driver board based on ULN2003APG darlington array
  RFID-RC522-v2: A simple China made RFID-RC522 Reader; do check the pin labels, as this is a MFRC522 based clone.
